# Fritzing sketch MatrixBoy (saved by Fritzing 0.9.4)
circuit board: 13.6551cm x 10.2252cm
breadboards: 2

parts:
  Composant1 = Arduino Nano (Rev3.0) (ICSP)
  SPKR1 = Loudspeaker
  Disp1 = LBT2088AH [part_number=LBT2088AH]
  R1 = Resistor [tolerance=±5% resistance=220 package=THT]
  S1 = SWITCH-MOMENTARY-2 [package=tactile-pth-12mm]
  S2 = SWITCH-MOMENTARY-2 [package=tactile-pth-12mm]
  S3 = SWITCH-MOMENTARY-2 [package=tactile-pth-12mm]
  S4 = SWITCH-MOMENTARY-2 [package=tactile-pth-12mm]
  S5 = SWITCH-MOMENTARY-2 [package=tactile-pth-12mm]
  S6 = SWITCH-MOMENTARY-2 [package=tactile-pth-12mm]
  D4 = Rectifier Diode [part_number=1N4148 package="300 mil [THT]"]
  D2 = Rectifier Diode [part_number=1N4148 package="300 mil [THT]"]
  D3 = Rectifier Diode [part_number=1N4001 package="300 mil [THT]"]
  D5 = Rectifier Diode [part_number=1N4148 package="300 mil [THT]"]
  D6 = Rectifier Diode [part_number=1N4148 package="300 mil [THT]"]
  D1 = Rectifier Diode [part_number=1N4001 package="300 mil [THT]"]

nets:
  N1: Composant1.GND, SPKR1.pin1
  N2: Composant1.D2, Disp1.pin_9
  N3: Composant1.D3, Disp1.pin_7
  N4: Composant1.D4, Disp1.pin_8
  N5: Composant1.D5, Disp1.pin_6, S4.1
  N6: Composant1.D6, Disp1.pin1
  N7: Composant1.D7, Disp1.pin2
  N8: Composant1.D8, Disp1.pin_10, S5.1
  N9: Composant1.D9, Disp1.pin_5
  N10: Composant1.D10, Disp1.pin_4, S6.1
  N11: Composant1.D11/MOSI, SPKR1.pin2
  N12: Composant1.D12/MISO, Disp1.pin_3
  N13: Composant1.5V, R1.Pin_0
  N14: Composant1.A6, R1.Pin_1, D4.anode, D2.anode, D3.anode, D5.anode, D6.anode, D1.anode
  N15: Composant1.A5, Disp1.pin_11, S3.1
  N16: Composant1.A4, Disp1.pin_12
  N17: Composant1.A3, Disp1.pin_13
  N18: Composant1.A2, Disp1.pin_14
  N19: Composant1.A1, Disp1.pin_15, S2.1
  N20: Composant1.A0, Disp1.pin_16, S1.1
  N21: S1.2, D1.cathode
  N22: S2.2, D2.cathode
  N23: S3.2, D3.cathode
  N24: S4.2, D4.cathode
  N25: S5.2, D5.cathode
  N26: S6.2, D6.cathode
